# Fritzing sketch WiresSketch (saved by Fritzing 0.9.3b)
breadboards: 3

parts:
  S1 = Round Pushbutton
  S2 = Round Pushbutton
  S3 = Round Pushbutton
  S4 = Round Pushbutton
  Part1 = Audio Jack Breakout
  LED1 = 7-SEGMENT-4DIGIT-YOUNGSUN [package=7-segment-4digit-youngsun]  # not connected
  J1 = Piezo Speaker
  Mod1 = Amica NodeMCU DevKit 1.0
  Disp1 = LBT2088AH [part_number=LBT2088AH]  # not connected
  Disp2 = LBT2088AH [part_number=LBT2088AH]
  Disp3 = LBT2088AH [part_number=LBT2088AH]  # not connected
  Disp4 = LBT2088AH [part_number=LBT2088AH]  # not connected
  M1 = pcf8574 io expansion board [package=THT]
  M2 = pcf8574 io expansion board [package=THT]
  S5 = Round Pushbutton  # not connected
  S6 = Round Pushbutton
  LED2 = smd LED [color="Red (633nm)" package="0805 [SMD]"]  # not connected
  LED3 = LED_RING [package=led_ring]
  U1 = WS2812 RGB LED matrix 1x8

nets:
  N1: S1.leg0, S2.leg0, S3.leg0, S4.leg0
  N2: Part1.RING_SHUNT, J1.pin1
  N3: Part1.RING, J1.pin2
  N4: Part1.TIP, S6.leg0
  N5: Mod1.pin1, Mod1.pin2, Mod1.pin3, Mod1.pin4, Mod1.pin6, Mod1.pin7, Mod1.pin8, Mod1.pin_9, Mod1.pin_10, Mod1.pin_12, Mod1.pin_13, Mod1.pin_14, Mod1.pin_15, Mod1.pin_16, Mod1.pin_17, Mod1.pin_18, Mod1.pin_19, Mod1.pin_21, Mod1.pin_22, Mod1.pin_23, Mod1.pin_24, Mod1.pin_25, Mod1.pin_26, Mod1.pin_27, Mod1.pin_28, Mod1.pin_29, Mod1.pin_30
  N6: Disp2.pin1, U1.DIN
  N7: Disp2.pin2, U1.VCC#1
  N8: Disp2.pin_3, U1.GND#0
  VCC: M1.VCC, M2.VCC
  GND: M1.GND, M2.GND
  N9: LED3.7, U1.GND#4
  N10: LED3.8, U1.VCC#5
  N11: LED3.9, U1.DOUT

notes:
  Legend:
  Red - Power
  Black - Ground
  Yellow - Button data
  Green{
  Matrix data, Wires data, Leds data }
  Purple - MP3 data
  Pink - Timer data1
  Grey - Timer data2
  Cyan - Speaker in
  Brown - Speaker out

custom parts:
  Amica NodeMCU DevKit 1.0: Amica NodeMCU DevKit 1.0 Development Kit based on ESP8266 ESP-12E, integating GPIO, PWM, IIC, 1-Wire and ADC all in one board. Links: NodeMCU information page Github
  pcf8574 io expansion board: pcf8574 io expansion board.
  WS2812 RGB LED matrix 1x8: WS2812 matrix 1x8
